# Fritzing sketch ServoBlume_MK1 (saved by Fritzing 0.9.10b)
circuit board: 6.578cm x 3.96975cm
breadboards: 1

parts:
  UNO = Arduino Uno (Rev3) - ICSP
  TM1638_-_Led_Button_Module1 = IC, DIP package, 10 pins [chip_label=TM1638]
  Servo_(PVG_Pinout) = Basic Servo
  BUTTON1 = Arcade Button (blue)
  C1 = Electrolytic Capacitor [capacitance=100µF voltage=35V package="100 mil [THT, electrolytic]"]
  Button_Connector = Screw terminal - 2 pins [package=THT]
  LED&KEY_Conncector = female pin header, 5 pins [form="♀ (female)"]
  Servo_(VPG)_Connector = female pin header, 3 pins [form="♀ (female)"]

nets:
  GND: UNO.GND, TM1638_-_Led_Button_Module1.pin2, Servo_(PVG_Pinout).gnd, BUTTON1.no_name_yet#2, C1.-, Button_Connector.pin2, LED&KEY_Conncector.pin4, Servo_(VPG)_Connector.pin3
  N1: UNO.D3_PWM, TM1638_-_Led_Button_Module1.pin3, LED&KEY_Conncector.pin3
  N2: UNO.D4, TM1638_-_Led_Button_Module1.pin4, LED&KEY_Conncector.pin2
  N3: UNO.D5_PWM, TM1638_-_Led_Button_Module1.pin5, LED&KEY_Conncector.pin1
  N4: UNO.D6_PWM, Servo_(PVG_Pinout).pulse, Servo_(VPG)_Connector.pin2
  N5: UNO.D7, BUTTON1.no_name_yet#1, Button_Connector.pin1
  5V: UNO.5V, TM1638_-_Led_Button_Module1.pin1, Servo_(PVG_Pinout).vcc, C1.+, LED&KEY_Conncector.pin5, Servo_(VPG)_Connector.pin1

custom parts:
  Arcade Button (blue): Adafruit Arcade Button (blue)
